# Fritzing sketch esquema (saved by Fritzing 0.7.11b)
breadboards: 1

parts:
  Arduino1 = Arduino
  LED1 = LED - 5mm [color="Red (633nm)" package="5 mm [THT]"]
  LED2 = LED - 5mm [color="Red (633nm)" package="5 mm [THT]"]
  LED3 = LED - 5mm [color="Red (633nm)" package="5 mm [THT]"]
  LED4 = LED - 5mm [color="Red (633nm)" package="5 mm [THT]"]
  LED5 = LED - 5mm [color="Red (633nm)" package="5 mm [THT]"]
  LED6 = LED - 5mm [color="Red (633nm)" package="5 mm [THT]"]
  LED7 = LED - 5mm [color="Red (633nm)" package="5 mm [THT]"]
  LED8 = LED - 5mm [color="Red (633nm)" package="5 mm [THT]"]
  LED9 = LED - 5mm [color="Red (633nm)" package="5 mm [THT]"]
  LED10 = LED - 5mm [color="Red (633nm)" package="5 mm [THT]"]
  R1 = Resistor [tolerance=±5% resistance=220 package=THT]
  R2 = Resistor [tolerance=±5% resistance=220 package=THT]
  R3 = Resistor [tolerance=±5% resistance=220 package=THT]
  R4 = Resistor [tolerance=±5% resistance=220 package=THT]
  R5 = Resistor [tolerance=±5% resistance=220 package=THT]
  R6 = Resistor [tolerance=±5% resistance=220 package=THT]
  R7 = Resistor [tolerance=±5% resistance=220 package=THT]
  R8 = Resistor [tolerance=±5% resistance=220 package=THT]
  R10 = Resistor [tolerance=±5% resistance=220 package=THT]
  R11 = Resistor [tolerance=±5% resistance=220 package=THT]
  R12 = Rotary Potentiometer (Small) [maximum_resistance=100kΩ]
  S1 = Pushbutton [package="[THT]"]
  R13 = Resistor [tolerance=±5% resistance=220 package=THT]

nets:
  N1: Arduino1.D12, S1.Pin_1, S1.Pin_2, R13.Pin_1
  N2: Arduino1.D11, LED10.anode
  N3: Arduino1.D10, LED9.anode
  N4: Arduino1.D9, LED8.anode
  N5: Arduino1.D8, LED7.anode
  N6: Arduino1.D7, LED6.anode
  N7: Arduino1.D6, LED5.anode
  N8: Arduino1.D5, LED4.anode
  N9: Arduino1.D4, LED3.anode
  N10: Arduino1.D3, LED2.anode
  N11: Arduino1.D2, LED1.anode
  N12: Arduino1.+5V, R12.leg2
  N13: Arduino1.GND, R1.Pin_0, R2.Pin_0, R3.Pin_0, R4.Pin_0, R5.Pin_0, R6.Pin_0, R7.Pin_0, R8.Pin_0, R10.Pin_0, R11.Pin_0, R12.leg1, S1.Pin_3, S1.Pin_4, R13.Pin_0
  N14: Arduino1.A0, R12.wiper
  N15: LED1.cathode, R1.Pin_1
  N16: LED2.cathode, R2.Pin_1
  N17: LED3.cathode, R8.Pin_1
  N18: LED4.cathode, R7.Pin_1
  N19: LED5.cathode, R6.Pin_1
  N20: LED6.cathode, R5.Pin_1
  N21: LED7.cathode, R4.Pin_1
  N22: LED8.cathode, R3.Pin_1
  N23: LED9.cathode, R11.Pin_1
  N24: LED10.cathode, R10.Pin_1
